// Logisim project LAB2.circ as structural Verilog: 1 circuit, main circuit main
module main (
  input  SW0
);

  wire and_1_out, and_2_out, and_3_out, clock_1_out, j_k_ff_1_q, j_k_ff_1_qn, j_k_ff_2_q, j_k_ff_3_q,
       j_k_ff_4_q;

  and and_1 (and_1_out, j_k_ff_3_q, j_k_ff_4_q);
  and and_2 (and_2_out, j_k_ff_2_q, j_k_ff_3_q, j_k_ff_4_q);
  LED led_1 (.in(j_k_ff_1_q));
  J_K_Flip_Flop j_k_ff_1 (
    .J(and_2_out), .clk(clock_1_out), .K(and_1_out), .Q(j_k_ff_1_q), .Qn(j_k_ff_1_qn), .preset(SW0),
    .reset(SW0));  // open: en
  LED led_2 (.in(j_k_ff_2_q));
  and and_3 (and_3_out, j_k_ff_1_qn, j_k_ff_3_q, j_k_ff_4_q);
  J_K_Flip_Flop j_k_ff_2 (
    .J(and_3_out), .clk(clock_1_out), .K(and_1_out), .Q(j_k_ff_2_q), .preset(SW0), .reset(SW0));  // open: Qn, en
  LED led_3 (.in(j_k_ff_3_q));
  J_K_Flip_Flop j_k_ff_3 (
    .J(j_k_ff_4_q), .clk(clock_1_out), .K(j_k_ff_4_q), .Q(j_k_ff_3_q), .preset(SW0), .reset(SW0));  // open: Qn, en
  LED led_4 (.in(j_k_ff_4_q));
  J_K_Flip_Flop j_k_ff_4 (
    .J(1'b1), .clk(clock_1_out), .K(1'b1), .Q(j_k_ff_4_q), .preset(SW0), .reset(SW0));  // open: Qn, en
  Clock clock_1 (.out(clock_1_out));

  // Notes on the sheet:
  //   D
  //   C
  //   B
  //   A
  //   CLK
endmodule
