// Logisim project Mô Phỏng BĐB.circ as structural Verilog: 1 circuit, main circuit main
module main (
  output D,
  output C,
  output B,
  output A
);

  wire clock_1_out, nand_1_out;

  J_K_Flip_Flop j_k_ff_1 (.J(1'b1), .clk(C), .K(1'b1), .Q(D), .reset(nand_1_out));  // open: Qn, preset, en
  nand nand_1 (nand_1_out, C, D);
  J_K_Flip_Flop j_k_ff_2 (.J(1'b1), .clk(B), .K(1'b1), .Q(C), .reset(nand_1_out));  // open: Qn, preset, en
  J_K_Flip_Flop j_k_ff_3 (.J(1'b1), .clk(A), .K(1'b1), .Q(B), .reset(nand_1_out));  // open: Qn, preset, en
  J_K_Flip_Flop j_k_ff_4 (.J(1'b1), .clk(clock_1_out), .K(1'b1), .Q(A), .reset(nand_1_out));  // open: Qn, preset, en
  Clock clock_1 (.out(clock_1_out));
endmodule
