// Logisim project Mạch Đếm Đồng Bộ 4 Bit Lab 2.circ as structural Verilog: 1 circuit, main circuit main
module main (
  input  in_1,
  output D,
  output C,
  output B,
  output A
);

  wire and_1_out, and_2_out, and_3_out, and_4_out, and_5_out, clock_1_out, j_k_ff_1_qn, j_k_ff_2_qn,
       j_k_ff_4_qn, or_1_out, or_2_out, or_3_out, or_4_out;

  and and_1 (and_1_out, A, B);
  J_K_Flip_Flop j_k_ff_1 (
    .J(B), .clk(clock_1_out), .K(and_1_out), .Q(D), .Qn(j_k_ff_1_qn), .preset(in_1), .reset(in_1));  // open: en
  and and_2 (and_2_out, j_k_ff_1_qn, B);
  or or_1 (or_1_out, and_2_out, and_4_out);
  and and_3 (and_3_out, A, j_k_ff_1_qn);
  and and_4 (and_4_out, B, A);
  or or_2 (or_2_out, and_3_out, B);
  J_K_Flip_Flop j_k_ff_2 (
    .J(or_2_out), .clk(clock_1_out), .K(or_1_out), .Q(C), .Qn(j_k_ff_2_qn), .preset(in_1), .reset(in_1));  // open: en
  and and_5 (and_5_out, j_k_ff_2_qn, j_k_ff_4_qn);
  or or_3 (or_3_out, D, C);
  or or_4 (or_4_out, A, and_5_out, j_k_ff_1_qn);
  J_K_Flip_Flop j_k_ff_3 (
    .J(or_3_out), .clk(clock_1_out), .K(or_4_out), .Q(B), .preset(in_1), .reset(in_1));  // open: Qn, en
  J_K_Flip_Flop j_k_ff_4 (
    .J(1'b1), .clk(clock_1_out), .K(or_3_out), .Q(A), .Qn(j_k_ff_4_qn), .preset(in_1), .reset(in_1));  // open: en
  Clock clock_1 (.out(clock_1_out));
endmodule
