// Logisim project Sơ Đồ Mạch BĐB.circ as structural Verilog: 1 circuit, main circuit main
module main (
);

  wire n7476_1_p2, n7476_1_p3, n7476_1_p4, n7476_1_p10, n7476_2_p4, n7476_2_p12;

  LED led_1 (.in(n7476_1_p3));
  // _7476 7476_1: pin names not known; wires that end beside it: 1'b1, n7476_1_p2, n7476_1_p3, n7476_1_p4, 1'b0, 1'b1, 1'b1, 1'b1, n7476_1_p2, n7476_1_p10
  LED led_2 (.in(n7476_1_p2));
  LED led_3 (.in(n7476_1_p10));
  // _7476 7476_2: pin names not known; wires that end beside it: 1'b1, n7476_1_p4, 1'b1, n7476_2_p4, n7476_1_p10, n7476_1_p4, 1'b0, 1'b1, 1'b1, 1'b1, n7476_2_p4, n7476_2_p12
  LED led_4 (.in(n7476_2_p4));
  Clock clock_1 (.out(n7476_2_p12));
  // _7400 7400_1: pin names not known; wires that end beside it: 1'b1, n7476_1_p4, 1'b1, n7476_1_p3, n7476_1_p2, n7476_1_p4, 1'b0

  // Notes on the sheet:
  //   VCC
  //   D
  //   C
  //   A
  //   B
  //   CLK
endmodule
